# Fritzing sketch BoxBeatsPhoton (saved by Fritzing 0.9.2b)
breadboards: 1

parts:
  Part1 = Photon
  NEOPIXEL1 = Neopixel Strip -- Black (60/m)
  NEOPIXEL2 = Neopixel Strip -- Black (60/m)

nets:
  GND: Part1.GND, NEOPIXEL1.GND, NEOPIXEL2.GND
  N1: Part1.D2, NEOPIXEL2.+5V
  N2: Part1.D3, NEOPIXEL1.+5V
  N3: Part1.3V3, NEOPIXEL1.DI, NEOPIXEL2.DI

custom parts:
  Neopixel Strip -- Black (60/m): Neopixel Strip, Black, 60 pixels per meter.
